# Fritzing sketch Test_setup_1 (saved by Fritzing 0.9.10b)
breadboards: 1

parts:
  RE1 = Rotary Encoder [package=THT]
  Bauteil1 = Arduino Uno (Rev3)
  R1 = Resistor [tolerance=±5% power=0.25 resistance=10k package=THT]
  R2 = Resistor [tolerance=±5% power=0.25 resistance=10k package=THT]

nets:
  N1: RE1.EncoderPinA, Bauteil1.D4, R2.Pin_0
  N2: RE1.EncoderPinC, Bauteil1.5V
  N3: RE1.EncoderPinB, Bauteil1.D2, R1.Pin_0
  N4: Bauteil1.GND, R1.Pin_1, R2.Pin_1
