# Fritzing sketch my_basic_code_pattern (saved by Fritzing 0.9.10b)
breadboards: 1

parts:
  Encoder = Rotary Encoder [package=THT]
  Bauteil1 = Arduino Uno (Rev3)
  R1 = Resistor [tolerance=±5% power=0.25 resistance=10k package=THT]
  R2 = Resistor [tolerance=±5% power=0.25 resistance=10k package=THT]
  Encoder_Press = Pushbutton [package="[THT]"]
  S1 = Pushbutton [package="[THT]"]
  S2 = Pushbutton [package="[THT]"]
  S3 = Pushbutton [package="[THT]"]
  Bauteil2 = NeoPixel Stick [part_number=1426]

nets:
  N1: Encoder.EncoderPinA, Bauteil1.D4, R2.Pin_0
  GND: Encoder.EncoderPinC, Bauteil1.GND, Encoder_Press.Pin_3, Encoder_Press.Pin_4, S1.Pin_1, S1.Pin_2, S2.Pin_1, S2.Pin_2, S3.Pin_1, S3.Pin_2, Bauteil2.GND
  N2: Encoder.EncoderPinB, Bauteil1.D2, R1.Pin_0
  N3: Bauteil1.D12/MISO, Bauteil2.DATAIN
  N4: Bauteil1.D3_PWM, S1.Pin_3, S1.Pin_4
  N5: Bauteil1.D5_PWM, Encoder_Press.Pin_1, Encoder_Press.Pin_2
  N6: Bauteil1.D6_PWM, S2.Pin_3, S2.Pin_4
  N7: Bauteil1.D7, S3.Pin_3, S3.Pin_4
  5V: Bauteil1.5V, R1.Pin_1, R2.Pin_1, Bauteil2.+5V

custom parts:
  NeoPixel Stick: Make your own little LED strip arrangement with this stick of NeoPixel LEDs. We crammed 8 of the tiny 5050 (5mm x 5mm) smart RGB LEDs onto a PCB with mounting holes and a chainable design. Use only one microcontroller pin to control as many as you can chain together! Each LED is addressable as the driver chip is inside the LED. Each one has ~18mA constant current drive so the color will be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
