# Fritzing sketch setup_for_pattern_development (saved by Fritzing 0.9.10b)
breadboards: 1

parts:
  RE1 = Rotary Encoder [package=THT]
  Bauteil1 = Arduino Uno (Rev3)
  R1 = Resistor [tolerance=±5% power=0.25 resistance=10k package=THT]
  R2 = Resistor [tolerance=±5% power=0.25 resistance=10k package=THT]
  S1 = Pushbutton [package="[THT]"]
  S2 = Pushbutton [package="[THT]"]
  S3 = Pushbutton [package="[THT]"]
  S4 = Pushbutton [package="[THT]"]

nets:
  N1: RE1.EncoderPinA, Bauteil1.D4, R2.Pin_0
  N2: RE1.EncoderPinC, Bauteil1.GND, S1.Pin_3, S1.Pin_4, S2.Pin_1, S2.Pin_2, S3.Pin_1, S3.Pin_2, S4.Pin_1, S4.Pin_2
  N3: RE1.EncoderPinB, Bauteil1.D2, R1.Pin_0
  N4: Bauteil1.D8, S4.Pin_3, S4.Pin_4
  N5: Bauteil1.D5_PWM, S1.Pin_1, S1.Pin_2
  N6: Bauteil1.D6_PWM, S2.Pin_3, S2.Pin_4
  N7: Bauteil1.D7, S3.Pin_3, S3.Pin_4
  N8: Bauteil1.5V, R1.Pin_1, R2.Pin_1
